// Logisim project cpu.circ as structural Verilog: 1 circuit, main circuit cpu
module cpu (
  input  clk,
  input  [31:0] INSTRUCTION,
  input  [31:0] READ_DATA,
  output [31:0] WRITE_ADDRESS,
  output [31:0] PROGRAM_COUNTER,
  output [31:0] ra,
  output [31:0] sp,
  output [31:0] t0,
  output [31:0] t1,
  output [31:0] t2,
  output [31:0] s0,
  output [31:0] s1,
  output [31:0] a0,
  output [31:0] tohost,
  output [3:0] WRITE_ENABLE,
  output [31:0] WRITE_DATA
);

  wire Asel, Bsel, regfile_1_p7, regfile_1_p8, regfile_1_p10, regfile_1_p19, regfile_1_p21, regfile_1_p23,
       regwe;
  wire [2:0] funct3, immsel;
  wire [3:0] ALUsel;
  wire [6:0] funct7;
  wire [24:0] INSTRUCTION_after;
  wire [31:0] adder_1_out, alu1, imm, PROGRAM_COUNTER_after, rs1_data, rs2_data;

  Adder #(.width(32)) adder_1 (.a(PROGRAM_COUNTER), .b(32'h4), .out(adder_1_out));  // open: cin, cout
  Register #(.width(32)) PC (.D(adder_1_out), .en(1'b1), .clk(clk), .Q(PROGRAM_COUNTER));  // open: clr
  Register #(.width(32)) register_1 (
    .D(INSTRUCTION), .en(1'b1), .clk(clk),
    .Q({funct7, INSTRUCTION_after[24:15], funct3, INSTRUCTION_after[11:0]}));  // open: clr
  Register #(.width(32)) register_2 (
    .D(PROGRAM_COUNTER), .en(1'b1), .clk(clk), .Q(PROGRAM_COUNTER_after));  // open: clr
  control_logic control_logic_1 (
    .RegWEn(regwe), .ImmSel(immsel), .ASel(Asel), .BSel(Bsel), .ALUSel(ALUsel),
    .inst({funct7, INSTRUCTION_after[24:15], funct3, INSTRUCTION_after[11:0]}));  // open: CSRWen, PCSel, BrUn, MemRW, WBSel, CSRSel, BrEq, BrLt
  imm_gen imm_gen_1 (
    .inst({funct7, INSTRUCTION_after[24:15], funct3, INSTRUCTION_after[11:0]}), .ImmSel(immsel), .imm(imm));
  // regfile regfile_1: pin names not known; wires that end beside it: INSTRUCTION_after[19:15], INSTRUCTION_after[24:20], INSTRUCTION_after[11:7], alu1, regwe, clk, regfile_1_p7, regfile_1_p8, regfile_1_p8, regfile_1_p10, regfile_1_p10, ra, sp, t0, t1, t2, s0, s1, regfile_1_p19, regfile_1_p19, regfile_1_p21, regfile_1_p21, regfile_1_p23
  // branch_comp branch_comp_1: pin names not known; wires that end beside it: a0, rs1_data, rs2_data
  // alu alu_1: pin names not known; wires that end beside it: rs1_data, imm, ALUsel, alu1
  csr csr_1 (.tohost(tohost));  // open: CSR_address, CSR_din, CSR_WE, clk

  // Other names for the same wires on the sheet: opcode[6:0] = INSTRUCTION_after[6:0];
  //   rd[4:0] = INSTRUCTION_after[11:7]; INSTRUCTION_after (some bits) = {funct7, funct3};
  //   rs1[4:0] = INSTRUCTION_after[19:15]; rs2[4:0] = INSTRUCTION_after[24:20]

  // Notes on the sheet:
  //   Output to IMEM
  //   IMEM (do **NOT** move this)
  //   Inputs from IMEM
  //   It is OK to move the PC, RegFile, ALU, MEM, Branch Comp, Imm Gen, and Control Logic to wherever is most convenient for you when constructing your CPU, and to delete this text
  //   Inputs/Outputs for testing. Do **NOT** move these.
  //   Outputs To DMEM
  //   DMEM (do **NOT** move this)
  //   Inputs From DMEM
endmodule
