// Logisim project imm_gen.circ as structural Verilog: 1 circuit, main circuit imm_gen
module imm_gen (
  input  [31:0] inst,
  input  [2:0] ImmSel,
  output [31:0] imm
);

  wire [31:0] b_type, I_type, s_type;
  wire [31:20] j_type;

  assign I_type = {{20{inst[31]}}, inst[31:20]};  // Bit_Extender bit_extender_1
  assign s_type = {{20{inst[31]}}, {inst[31:25], inst[11:7]}};  // Bit_Extender bit_extender_2
  assign j_type = {{11{inst[31]}}, inst[31]};  // Bit_Extender bit_extender_3
  assign b_type = {{19{inst[31]}}, {inst[31], inst[7], inst[30:25], inst[11:8], 1'b0}};  // Bit_Extender bit_extender_4
  Multiplexer #(.enable("false"), .select(3), .width(32)) multiplexer_1 (
    .in0(I_type), .in1(s_type), .in2(b_type), .in3({inst[31:12], {12{1'b0}}}),
    .in4({j_type, inst[19:12], inst[20], inst[30:21], 1'b0}), .out(imm), .sel(ImmSel));  // open: in5, in6, in7

  // Other names for the same wires on the sheet: u_type[31:12] = inst[31:12];
  //   j_type[19:1] = {inst[19:12], inst[20], inst[30:21]}

  // Notes on the sheet:
  //   INPUTS to your circuit
  //   DON'T CHANGE THE LOCATIONS OF THE INPUTS AND OUTPUTS!
  //   OUTPUT from your circuit
endmodule
